# Fritzing sketch PCR Fritzing File (saved by Fritzing 0.9.4)
circuit board: 8.46667cm x 5.64444cm
breadboards: 1

parts:
  Part1 = Arduino Uno (Rev3)
  Part2 = Adafruit Analog 2-Axis Joystick [part_number="Adafruit #512"]
  LCM1602_IIC2 = LCM1602 IIC [part_number="LCM1602 IIC" chip_label="LCM1602 IIC" package="DIP (Dual Inline) [THT]"]
  LCD1 = LCD screen
  Part3 = Adafruit Thermocouple Amplifier MAX31855 [part_number="Adafruit #269"]

nets:
  N1: Part1.A0, Part2.XOUT
  N2: Part1.A1, Part2.YOUT
  N3: Part1.A4/SDA, LCM1602_IIC2.SDA
  N4: Part1.A5/SCL, LCM1602_IIC2.SCL
  N5: Part1.D2, Part2.SWITCH
  N6: Part1.D3_PWM, Part3.DO
  N7: Part1.D4, Part3.CS
  N8: Part1.D5_PWM, Part3.CLK
  VCC: Part1.5V, Part2.VCC, LCM1602_IIC2.VCC, Part3.VIN
  GND: Part1.GND, Part2.GND, LCM1602_IIC2.GND, Part3.GND
  VSS: LCM1602_IIC2.VSS, LCD1.VSS
  VDD: LCM1602_IIC2.VDD, LCD1.VDD
  N9: LCM1602_IIC2.V0, LCD1.V0
  N10: LCM1602_IIC2.RS, LCD1.RS
  N11: LCM1602_IIC2.RW, LCD1.R/W
  N12: LCM1602_IIC2.E, LCD1.E
  N13: LCM1602_IIC2.D0, LCD1.DB0
  N14: LCM1602_IIC2.D1, LCD1.DB1
  N15: LCM1602_IIC2.D2, LCD1.DB2
  N16: LCM1602_IIC2.D3, LCD1.DB3
  N17: LCM1602_IIC2.D4, LCD1.DB4
  N18: LCM1602_IIC2.D5, LCD1.DB5
  N19: LCM1602_IIC2.D6, LCD1.DB6
  N20: LCM1602_IIC2.D7, LCD1.DB7
  N21: LCM1602_IIC2.A, LCD1.LED+
  N22: LCM1602_IIC2.K, LCD1.LED-

custom parts:
  Adafruit Analog 2-Axis Joystick: This mini-kit makes it easy to mount a PSP/Xbox-like thumb joystick to your project. The thumbstick is an analog joystick - more accurate and sensitive than just 'directional' joysticks - with a 'press in to select' button. Since it's analog, you'll need two analog reading pins on your microcontroller to determine X and Y. Having an extra digital input will let you read the switch. The pack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
  LCM1602 IIC: I2C-Module to use a 1602 or 2004 LCD on with the wire.h libory Serial LCD Modul
  Adafruit Thermocouple Amplifier MAX31855: Thermocouples are very sensitive, requiring a good amplifier with a cold-compensation reference. The MAX31855K does everything for you, and can be easily interfaced with any microcontroller, even one without an analog input. This breakout board has the chip itself, a 3.3V regulator with 10uF bypass capacitors and level shifting circuitry, all assembled and tested. Comes with a 2 pin terminal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
